// Logisim project 11.circ as structural Verilog: 1 circuit, main circuit main
module main (
  input  in_1,
  input  in_2,
  input  in_3,
  output out_4,
  output out_5
);

  wire and_1_out, and_2_out, undriven, undriven_2, undriven_3, xor_1_out;

  xor xor_1 (xor_1_out, undriven_2, undriven);
  and and_1 (and_1_out, xor_1_out, undriven_3);
  and and_2 (and_2_out, undriven_2, undriven);
  xor xor_2 (out_4, xor_1_out, undriven_3);
  or or_1 (out_5, and_1_out, and_2_out);
endmodule
