// Logisim project Ejercicio13.circ as structural Verilog: 1 circuit, main circuit main
module main (
  input  e3,
  input  e2,
  input  e1,
  input  e0,
  output out_5,
  output out_6,
  output out_7,
  output out_8
);

  not not_1 (out_5, e0);
  not not_2 (out_6, e1);
  not not_3 (out_7, e2);
  not not_4 (out_8, e3);
endmodule
