// Logisim project Ejericicio 4.circ as structural Verilog: 1 circuit, main circuit main
module main (
  input  in_1,
  input  in_2,
  input  in_3,
  output out_4,
  output out_5
);

  wire nand_1_out;

  nand nand_1 (nand_1_out, in_1, in_2);
  nand nand_2 (out_5, in_3, in_3);
  nand nand_3 (out_4, nand_1_out, nand_1_out);
endmodule
