// Logisim project TallerLogica-Combinatorios.circ as structural Verilog
// Sumador simple
module sumador_simple (
  input  a,
  input  b,
  output S,
  output Cout
);

  xor xor_1 (S, a, b);
  and and_1 (Cout, a, b);
endmodule

// Sumador completo
module sumador_completo (
  input  Cin,
  input  A,
  input  B,
  output S,
  output Cout
);

  wire sumador_simple_1_cout, sumador_simple_1_s, sumador_simple_2_cout;

  sumador_simple sumador_simple_1 (.a(A), .b(B), .S(sumador_simple_1_s), .Cout(sumador_simple_1_cout));
  sumador_simple sumador_simple_2 (.a(Cin), .b(sumador_simple_1_s), .S(S), .Cout(sumador_simple_2_cout));
  or or_1 (Cout, sumador_simple_1_cout, sumador_simple_2_cout);
endmodule

// Sumador 4
module sumador_4 (
  input  Cin,
  input  [3:0] A,
  input  [3:0] B,
  output [3:0] S,
  output Cout
);

  wire _2_cout, sumador_completo_1_cout, sumador_completo_2_cout;

  sumador_completo sumador_completo_1 (.A(B[0]), .B(A[0]), .Cin(Cin), .S(S[0]), .Cout(sumador_completo_1_cout));
  sumador_completo sumador_completo_2 (
    .A(A[1]), .B(B[1]), .Cin(sumador_completo_1_cout), .S(S[1]), .Cout(sumador_completo_2_cout));
  sumador_completo _2 (.A(A[2]), .B(B[2]), .Cin(sumador_completo_2_cout), .S(S[2]), .Cout(_2_cout));
  sumador_completo _3 (.A(A[3]), .B(B[3]), .Cin(_2_cout), .S(S[3]), .Cout(Cout));
  Hex_Digit_Display hex_digit_display_1 (.value(S));  // open: dp
endmodule

module comparador_cero (
  input  [3:0] A,
  output Z
);

  wire not_1_out, not_2_out, not_3_out, not_4_out;

  not not_1 (not_1_out, A[0]);
  not not_2 (not_2_out, A[1]);
  not not_3 (not_3_out, A[2]);
  not not_4 (not_4_out, A[3]);
  and and_1 (Z, not_1_out, not_2_out, not_3_out, not_4_out);
endmodule

// Sumador flags
module sumador_flags (
  input  Cin,
  input  [3:0] A,
  input  [3:0] B,
  output [3:0] S,
  output N,
  output Z,
  output V,
  output C
);

  wire and_1_out, and_2_out, not_1_out, not_2_out, not_3_out;

  sumador_4 sumador_4_1 (.Cin(Cin), .A(A), .S({N, S[2:0]}), .B(B), .Cout(C));
  not not_1 (not_1_out, A[3]);
  not not_2 (not_2_out, B[3]);
  not not_3 (not_3_out, N);
  and and_1 (and_1_out, not_1_out, N, not_2_out);
  and and_2 (and_2_out, A[3], not_3_out, B[3]);
  Hex_Digit_Display hex_digit_display_1 (.value({N, S[2:0]}));  // open: dp
  comparador_cero comparador_cero_1 (.A({N, S[2:0]}), .Z(Z));
  or or_1 (V, and_2_out, and_1_out);

  assign S[3] = N;
endmodule

// Incrementador 4
module incrementador_4 (
  input  [3:0] A,
  output [3:0] S
);

  sumador_4 sumador_4_1 (.Cin(1'b0), .A(A), .S(S), .B(4'b0001));  // open: Cout
  Hex_Digit_Display hex_digit_display_1 (.value(S));  // open: dp
endmodule

// inversor 4
module inversor_4 (
  input  [3:0] A,
  input  INV,
  output [3:0] S
);

  wire [3:0] incrementador_4_1_s, Not_4_s;

  Not_4 Not_4 (.A(A), .S(Not_4_s));
  incrementador_4 incrementador_4_1 (.A(Not_4_s), .S(incrementador_4_1_s));
  Multiplexer #(.width(4)) multiplexer_1 (.in0(A), .in1(incrementador_4_1_s), .out(S), .sel(INV));  // open: en
  Hex_Digit_Display hex_digit_display_1 (.value(S));  // open: dp
endmodule

module ALU (
  input  [3:0] A,
  input  [3:0] B,
  input  [1:0] OP,
  output N,
  output Z,
  output V,
  output C,
  output [3:0] S
);

  wire [3:0] and_4_1_n, or_4_1_n, restador_flags_1_s, sumador_flags_1_s;
  wire [3:2] multiplexer_2_out;

  sumador_flags sumador_flags_1 (.A(A), .B(B), .Cin(1'b0), .S(sumador_flags_1_s));  // open: N, Z, V, C
  Restador_flags restador_flags_1 (.A(A), .B(B), .S(restador_flags_1_s));  // open: N, Z, V, C
  And_4 and_4_1 (.A(A), .B(B), .N(and_4_1_n[0]));  // open: Z, S
  OR_4 or_4_1 (.A(A), .B(B), .N(or_4_1_n[0]));  // open: Z, S
  flags flags_1 (.A(S), .N(N));  // open: Z
  Multiplexer #(.select(2), .width(4)) multiplexer_1 (
    .in0(sumador_flags_1_s), .in1(restador_flags_1_s), .in2(and_4_1_n), .in3(or_4_1_n), .out(S), .sel(OP),
    .en(1'b1));
  Multiplexer #(.select(2), .width(4)) multiplexer_2 (.out({multiplexer_2_out, C, V}));  // open: in0, in1, in2, in3, sel, en
  Hex_Digit_Display hex_digit_display_1 (.value(S));  // open: dp
  // Pins of 1 and 4 bits meet at or_4_1_n
  // Pins of 1 and 4 bits meet at and_4_1_n
  // Pins of 2 and 4 bits meet at {multiplexer_2_out, C, V}
endmodule

module verificador (
  output [3:0] a,
  output [3:0] b,
  output [1:0] Op,
  output N,
  output Z,
  output V,
  output C,
  output [3:0] Res,
  output halt
);

  wire clock_1_out;

  Clock clock_1 (.out(clock_1_out));
  Counter #(.width(10), .max('h3ff)) counter_1 (
    .Q({Op, b, a}), .carry(halt), .clk(clock_1_out));  // open: load, D, count, clr
  ALU alu_1 (.A(a), .B(b), .OP(Op), .N(N), .Z(Z), .V(V), .C(C), .S(Res));
endmodule

module And_4 (
  input  [3:0] A,
  input  [3:0] B,
  output N,
  output Z,
  output [3:0] S
);

  and and_1 (N, A[0], B[0]);
  and and_2 (S[1], A[1], B[1]);
  and and_3 (S[2], A[2], B[2]);
  and and_4 (S[3], A[3], B[3]);
  comparador_cero comparador_cero_1 (.A({S[3:1], N}), .Z(Z));

  assign S[0] = N;
endmodule

module OR_4 (
  input  [3:0] A,
  input  [3:0] B,
  output N,
  output Z,
  output [3:0] S
);

  or or_1 (N, A[0], B[0]);
  or or_2 (S[1], A[1], B[1]);
  or or_3 (S[2], A[2], B[2]);
  or or_4 (S[3], A[3], B[3]);
  incrementador_flags incrementador_flags_1 ();

  assign S[0] = N;
endmodule

module Restador_flags (
  input  [3:0] A,
  input  [3:0] B,
  output [3:0] S,
  output N,
  output Z,
  output V,
  output C
);

  wire sumador_flags_1_c;
  wire [3:0] inversor_4_1_s;

  inversor_4 inversor_4_1 (.A(B), .S(inversor_4_1_s));  // open: INV
  sumador_flags sumador_flags_1 (
    .A(A), .B(inversor_4_1_s), .Cin(1'b0), .S(S), .N(N), .Z(Z), .V(V), .C(sumador_flags_1_c));
  not not_1 (C, sumador_flags_1_c);
endmodule

module flags (
  input  [3:0] A,
  output N,
  output Z
);

  incrementador_flags incrementador_flags_1 ();

  assign N = A[2];
endmodule

module Mayor_4 (
  input  [3:0] A,
  input  [3:0] B,
  output out_3
);

  wire igual_1_out_3, igual_2_out_3, igual_3_out_3, igual_4_out_3, Mayor_1_2_out_3, Mayor_1_3_out_3,
       Mayor_1_4_out_3, Mayor_1_out_3, or_1_out, or_2_out, or_3_out, or_4_out, or_5_out;

  Igual igual_1 (.A(A[0]), .B(B[0]), .out_3(igual_1_out_3));
  Mayor_1 Mayor_1 (.A(A[0]), .B(B[0]), .out_3(Mayor_1_out_3));
  Igual igual_2 (.A(A[1]), .B(B[1]), .out_3(igual_2_out_3));
  Mayor_1 Mayor_1_2 (.A(A[1]), .B(B[1]), .out_3(Mayor_1_2_out_3));
  Igual igual_3 (.A(A[2]), .B(B[2]), .out_3(igual_3_out_3));
  Mayor_1 Mayor_1_3 (.A(A[2]), .B(B[2]), .out_3(Mayor_1_3_out_3));
  Igual igual_4 (.A(A[3]), .B(B[3]), .out_3(igual_4_out_3));
  Mayor_1 Mayor_1_4 (.A(A[3]), .B(B[3]), .out_3(Mayor_1_4_out_3));
  or or_1 (or_1_out, igual_1_out_3, Mayor_1_out_3);
  or or_2 (or_2_out, igual_2_out_3, Mayor_1_2_out_3);
  or or_3 (or_3_out, igual_3_out_3, Mayor_1_3_out_3);
  or or_4 (or_4_out, igual_4_out_3, Mayor_1_4_out_3);
  or or_5 (or_5_out, or_1_out, or_2_out);
  // OR_Gate or_6 has open pins: in1=or_5_out, in3=or_3_out, out=open
endmodule

module Not_4 (
  input  [3:0] A,
  output [3:0] S
);

  not not_1 (S[0], A[0]);
  not not_2 (S[1], A[1]);
  not not_3 (S[2], A[2]);
  not not_4 (S[3], A[3]);
  Hex_Digit_Display hex_digit_display_1 (.value(S));  // open: dp
endmodule

module ALU_2 (
  input  [3:0] A,
  input  [3:0] B,
  input  [1:0] OP,
  output N,
  output Z,
  output V,
  output C,
  output [3:0] S
);

  sumador_flags sumador_flags_1 (.A(A), .B(B));  // open: Cin, S, N, Z, V, C
  Restador_flags restador_flags_1 ();  // open: A, B, S, N, Z, V, C
  And_4 and_4_1 ();  // open: A, B, N, Z, S
  OR_4 or_4_1 ();  // open: A, B, N, Z, S
  Multiplexer #(.select(2)) multiplexer_1 (.sel(OP));  // open: in0, in1, in2, in3, out, en
  Hex_Digit_Display hex_digit_display_1 (.value(S));  // open: dp
endmodule

module Igual (
  input  A,
  input  B,
  output out_3
);

  wire and_1_out, and_2_out, not_1_out, not_2_out;

  and and_1 (and_1_out, A, B);
  not not_1 (not_1_out, A);
  and and_2 (and_2_out, not_1_out, not_2_out);
  not not_2 (not_2_out, B);
  or or_1 (out_3, and_1_out, and_2_out);
endmodule

module Mayor_1 (
  input  A,
  input  B,
  output out_3
);

  wire not_1_out;

  not not_1 (not_1_out, A);
  and and_1 (out_3, not_1_out, B);
endmodule

module Igual_4 (
  input  [3:0] A,
  input  [3:0] B,
  output out_3
);

  wire igual_1_out_3, igual_2_out_3, igual_3_out_3, igual_4_out_3;

  Igual igual_1 (.A(A[0]), .B(B[0]), .out_3(igual_1_out_3));
  Igual igual_2 (.A(B[1]), .B(A[1]), .out_3(igual_2_out_3));
  Igual igual_3 (.A(A[2]), .B(B[2]), .out_3(igual_3_out_3));
  Igual igual_4 (.A(A[3]), .B(B[3]), .out_3(igual_4_out_3));
  and and_1 (out_3, igual_1_out_3, igual_2_out_3, igual_3_out_3, igual_4_out_3);
endmodule
