// Logisim project TallerLogica-Combinatorios1.circ as structural Verilog: 12 circuits, main circuit sumador_simple
// Sumador simple
module sumador_simple (
  input  a,
  input  b,
  output S,
  output Cout
);

  xor xor_1 (S, a, b);
  and and_1 (Cout, a, b);
endmodule

// Sumador completo
module sumador_completo (
  input  Cin,
  input  A,
  input  B,
  output S,
  output Cout
);

  wire sumador_simple_1_cout, sumador_simple_1_s, sumador_simple_2_cout;

  sumador_simple sumador_simple_1 (.a(A), .b(B), .S(sumador_simple_1_s), .Cout(sumador_simple_1_cout));
  sumador_simple sumador_simple_2 (.a(Cin), .b(sumador_simple_1_s), .S(S), .Cout(sumador_simple_2_cout));
  or or_1 (Cout, sumador_simple_1_cout, sumador_simple_2_cout);
endmodule

// Sumador 4
module sumador_4 (
  input  Cin,
  input  [3:0] A,
  input  [3:0] B,
  output [3:0] S,
  output Cout
);

  wire _0_cout, _1_cout, _2_cout;

  sumador_completo _0 (.A(B[0]), .B(A[0]), .Cin(Cin), .S(S[0]), .Cout(_0_cout));
  sumador_completo _1 (.A(A[1]), .B(B[1]), .Cin(_0_cout), .S(S[1]), .Cout(_1_cout));
  sumador_completo _2 (.A(A[2]), .B(B[2]), .Cin(_1_cout), .S(S[2]), .Cout(_2_cout));
  sumador_completo _3 (.A(A[3]), .B(B[3]), .Cin(_2_cout), .S(S[3]), .Cout(Cout));
  Hex_Digit_Display hex_digit_display_1 (.value(S));  // open: dp
endmodule

module comparador_cero (
  input  [3:0] A,
  output Z
);

  wire not_1_out, not_2_out, not_3_out, not_4_out;

  not not_1 (not_1_out, A[0]);
  not not_2 (not_2_out, A[1]);
  not not_3 (not_3_out, A[2]);
  not not_4 (not_4_out, A[3]);
  and and_1 (Z, not_1_out, not_2_out, not_3_out, not_4_out);
endmodule

// Sumador flags
module sumador_flags (
  input  Cin,
  input  [3:0] A,
  input  [3:0] B,
  output [3:0] S,
  output N,
  output Z,
  output V,
  output C
);

  wire and_1_out, and_2_out, not_1_out, not_2_out, not_3_out;

  sumador_4 sumador_4_1 (.Cin(Cin), .A(A), .S({N, S[2:0]}), .B(B), .Cout(C));
  not not_1 (not_1_out, A[3]);
  not not_2 (not_2_out, B[3]);
  not not_3 (not_3_out, N);
  and and_1 (and_1_out, not_1_out, N, not_2_out);
  and and_2 (and_2_out, A[3], not_3_out, B[3]);
  Hex_Digit_Display hex_digit_display_1 (.value({N, S[2:0]}));  // open: dp
  comparador_cero comparador_cero_1 (.A({N, S[2:0]}), .Z(Z));
  or or_1 (V, and_2_out, and_1_out);

  assign S[3] = N;
endmodule

// Incrementador 4
module incrementador_4 (
  input  [3:0] A,
  output [3:0] S
);

  sumador_4 sumador_4_1 (.Cin(1'b0), .A(A), .S(S), .B(4'b0001));  // open: Cout
  Hex_Digit_Display hex_digit_display_1 (.value(S));  // open: dp
endmodule

// inversor 4
module inversor_4 (
  input  [3:0] A,
  input  INV,
  output [3:0] S
);

  wire [3:0] xor_1_out;

  xor xor_1 (xor_1_out[0], A[0], INV);
  xor xor_2 (xor_1_out[1], A[1], INV);
  xor xor_3 (xor_1_out[2], INV, A[2]);
  xor xor_4 (xor_1_out[3], A[3], INV);
  sumador_4 sumador_4_1 (.Cin(INV), .A(xor_1_out), .S(S), .B(4'b0000));  // open: Cout
  Hex_Digit_Display hex_digit_display_1 (.value(S));  // open: dp
endmodule

module ALU (
  input  [3:0] A,
  input  [3:0] B,
  input  [1:0] OP,
  output N,
  output Z,
  output V,
  output C,
  output [3:0] S
);

  wire [1:0] restador_flags_1_v, sumador_flags_1_v;
  wire [3:0] and_4_1_s, or_4_1_s, restador_flags_1_s, sumador_flags_1_s;

  Hex_Digit_Display hex_digit_display_1 (.value(A));  // open: dp
  sumador_flags sumador_flags_1 (
    .A(A), .B(B), .Cin(1'b0), .S(sumador_flags_1_s), .V(sumador_flags_1_v[0]), .C(sumador_flags_1_v[1]));  // open: N, Z
  restador_flags restador_flags_1 (
    .A(A), .B(B), .S(restador_flags_1_s), .V(restador_flags_1_v[0]), .C(restador_flags_1_v[1]));  // open: N, Z
  and_4 and_4_1 (.A(A), .B(B), .S(and_4_1_s));
  or_4 or_4_1 (.A(A), .B(B), .S(or_4_1_s));
  Multiplexer #(.select(2), .width(4)) multiplexer_1 (
    .in0(sumador_flags_1_s), .in1(restador_flags_1_s), .in2(and_4_1_s), .in3(or_4_1_s), .out(S), .sel(OP),
    .en(1'b1));
  flags flags_1 (.A(S), .N(N), .Z(Z));
  Multiplexer #(.select(2), .width(2)) multiplexer_2 (
    .in0(sumador_flags_1_v), .in1(restador_flags_1_v), .in2(2'b00), .in3(2'b00), .out({C, V}), .sel(OP),
    .en(1'b1));
endmodule

module and_4 (
  input  [3:0] A,
  input  [3:0] B,
  output [3:0] S
);

  and and_1 (S[0], A[0], B[0]);
  and and_2 (S[1], A[1], B[1]);
  and and_3 (S[2], A[2], B[2]);
  and and_4 (S[3], A[3], B[3]);
endmodule

module or_4 (
  input  [3:0] A,
  input  [3:0] B,
  output [3:0] S
);

  or or_1 (S[0], A[0], B[0]);
  or or_2 (S[1], A[1], B[1]);
  or or_3 (S[2], A[2], B[2]);
  or or_4 (S[3], A[3], B[3]);
endmodule

module restador_flags (
  input  [3:0] A,
  input  [3:0] B,
  output [3:0] S,
  output N,
  output Z,
  output V,
  output C
);

  wire and_1_out, comparador_cero_1_z, distinto_signo_out, mismo_signo_out, not_1_out, not_2_out, not_3_out,
       sumador_flags_1_c;
  wire [3:0] inversor_4_1_s;

  inversor_4 inversor_4_1 (.A(B), .INV(1'b1), .S(inversor_4_1_s));
  sumador_flags sumador_flags_1 (
    .A(A), .B(inversor_4_1_s), .Cin(1'b0), .S(S), .N(N), .Z(Z), .V(V), .C(sumador_flags_1_c));
  xor distinto_signo (distinto_signo_out, A[3], B[3]);
  xor mismo_signo (mismo_signo_out, B[3], S[3]);
  not not_1 (not_1_out, mismo_signo_out);
  and and_1 (and_1_out, distinto_signo_out, not_1_out);
  Hex_Digit_Display hex_digit_display_1 (.value(S));  // open: dp
  not not_2 (not_2_out, sumador_flags_1_c);
  and and_2 (C, not_2_out, not_3_out);
  not not_3 (not_3_out, comparador_cero_1_z);
  comparador_cero comparador_cero_1 (.A(B), .Z(comparador_cero_1_z));
endmodule

module flags (
  input  [3:0] A,
  output N,
  output Z
);

  comparador_cero comparador_cero_1 (.A(A), .Z(Z));

  assign N = A[3];
endmodule
